# Fritzing sketch 06 (saved by Fritzing 0.9.3b)
breadboards: 1

parts:
  Part1 = Arduino Nano (Rev3.0)
  S1 = Pushbutton [package="[THT]"]
  R2 = Resistor [tolerance=±5% resistance=10k package=THT]
  R3 = Rotary Potentiometer (Small) [maximum_resistance=100kΩ package=THT]
  LED1 = LED - 5mm [color="Red (633nm)" package="5 mm [THT]"]
  LED2 = LED - 5mm [color="Red (633nm)" package="5 mm [THT]"]
  LED3 = LED - 5mm [color="Red (633nm)" package="5 mm [THT]"]
  LED4 = LED - 5mm [color="Red (633nm)" package="5 mm [THT]"]
  J1 = Piezo Speaker
  R4 = Resistor [tolerance=±5% resistance=220 package=THT]
  R5 = Resistor [tolerance=±5% resistance=220 package=THT]
  R6 = Resistor [tolerance=±5% resistance=220 package=THT]
  R7 = Resistor [tolerance=±5% resistance=220 package=THT]
  R8 = Rotary Potentiometer (Small) [maximum_resistance=100kΩ package=THT]

nets:
  N1: Part1.GND, R2.Pin_0, R3.leg2, LED1.cathode, LED2.cathode, LED3.cathode, LED4.cathode, J1.pin1, R8.leg2
  N2: Part1.D3, S1.Pin_1, S1.Pin_2, R2.Pin_1
  N3: Part1.D5, R4.Pin_1
  N4: Part1.D6, R5.Pin_1
  N5: Part1.D7, R6.Pin_1
  N6: Part1.D8, R7.Pin_1
  N7: Part1.D9, J1.pin2
  N8: Part1.5V, S1.Pin_3, S1.Pin_4, R3.leg1, R8.leg1
  N9: Part1.A6, R3.wiper
  N10: Part1.A5, R8.wiper
  N11: LED1.anode, R4.Pin_0
  N12: LED2.anode, R5.Pin_0
  N13: LED3.anode, R6.Pin_0
  N14: LED4.anode, R7.Pin_0
