# Fritzing sketch 07 (saved by Fritzing 0.9.3b)
breadboards: 1

parts:
  Part1 = Arduino Nano (Rev3.0)
  R1 = Photocell (LDR) [package=THT]
  R2 = Resistor [tolerance=±5% resistance=10k package=THT]
  R3 = Rotary Potentiometer (Small) [maximum_resistance=100kΩ package=THT]
  LED1 = RGB LED (com. cathode, rgb) [package="5 mm [THT]"]
  R4 = Resistor [tolerance=±5% resistance=1k package=THT]
  R5 = Resistor [tolerance=±5% resistance=1k package=THT]
  R6 = Resistor [tolerance=±5% resistance=1k package=THT]
  T1 = LM35 Temperature Sensor [package="TO92 [THT]"]

nets:
  GND: Part1.GND, R2.Pin_1, R3.leg2, T1.GND
  N1: Part1.5V, R1.pin_0, R3.leg1, T1.+Vs
  N2: Part1.A7, R3.wiper
  N3: Part1.A6, LED1.blue_anode, R6.Pin_0, R6.Pin_1
  N4: Part1.A5, R1.pin_1, R2.Pin_0
  N5: Part1.A4, LED1.green_anode, R5.Pin_0, R5.Pin_1
  N6: Part1.A3, T1.Vout
  N7: Part1.A2, LED1.red_anode, R4.Pin_0, R4.Pin_1
