# Fritzing sketch garden (saved by Fritzing 0.9.3b)
breadboards: 1

parts:
  KY-5 = Keyes Relay [package=THT]
  Part2 = Arduino Nano (Rev3.0)
  M1 = DC Motor

nets:
  N1: KY-5.signal, Part2.D3
  N2: KY-5.power, Part2.5V
  N3: KY-5.ground, Part2.GND, M1.pin_2
  N4: Part2.D8, M1.pin_1

notes:
  Power line entry
  Power line To the lamp
  Ground

custom parts:
  Keyes Relay: The Keyes 5V relay module is suitable for SCM development, home appliance control. It uses a 5V~12V TIL control signal which can control DC / AC signal.
